# Fritzing sketch Estacao_Repetidora-GPS (saved by Fritzing 0.9.3b)
breadboards: 2

parts:
  CPU1 = NodeMCU WROOM ESP 32
  A1 = RYLR998 [package=THT]
  S1 = Pushbutton [package="[SMD]"]
  OLED1 = SSD1306 0,96" OLED 128x64 I2C
  R1 = Resistor [tolerance=±5% resistance=220 package=THT]
  LED1 = LED - 5mm [color="Red (633nm)" package="5 mm [THT]"]
  R2 = Resistor [tolerance=±5% resistance=220 package=THT]
  LED2 = LED - 5mm [color="Yellow (595nm)" package="5 mm [THT]"]
  GY-NEO6MV1 = GY-NEO6MV2

nets:
  N1: CPU1.pin_7, GY-NEO6MV1.Rx
  N2: CPU1.pin_8, CPU1.pin_24, CPU1.pin_28, GY-NEO6MV1.Tx
  N3: CPU1.pin_9, CPU1.pin_25, S1.Pin_1, S1.Pin_2
  N4: CPU1.pin_10, LED2.anode
  N5: CPU1.pin_12, LED1.anode
  N6: CPU1.pin_15, GY-NEO6MV1.Vcc
  N7: CPU1.pin_16, GY-NEO6MV1.GND
  N8: CPU1.pin_17, A1.pin1, OLED1.VDD
  N9: CPU1.pin_18, A1.pin5, S1.Pin_3, S1.Pin_4, OLED1.GND, R1.Pin_0, R2.Pin_0
  N10: CPU1.pin_22, A1.pin4
  N11: CPU1.pin_23, A1.pin3
  N12: CPU1.pin_27, OLED1.SDA
  N13: CPU1.pin_30, OLED1.SCK
  N14: R1.Pin_1, R2.Pin_1, LED2.cathode

custom parts:
  NodeMCU WROOM ESP 32: 30 pol Development Kit
  RYLR998: The RYLR998 transceiver module feature the Lora long range modem that provides ultra-long range spread spectrum communication and high interference immunity whilst minimizing current consumption.
  SSD1306 0,96" OLED 128x64 I2C: YUS
  GY-NEO6MV2: Description: Module GPS , type GY-NEO6MV2, pour arduino et autres micro-contrôleurs. Caractéristiques De type GY-NEO6MV2 Alimentation 3V-5V Avec Flight Control EEPROM MWC Antenne large céramique, fort signal, 25 x 25 mm Paramètres de configuration sauvegardés en EEPROM Avec batterie de backup de données LED témoin de signal Module miniaturisé 25 x 35 mm Trou de fixation de 3mm Baud rate par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
